# Fritzing sketch schema_Projet (saved by Fritzing 0.9.3b)
breadboards: 1

parts:
  Composant1 = Arduino ProtoScrew Shield Kit
  R1 = Resistor [tolerance=±5% resistance=220 package=THT]
  R2 = Resistor [tolerance=±5% resistance=220 package=THT]
  R3 = Resistor [tolerance=±5% resistance=220 package=THT]
  LED1 = RGB LED (com. cathode, rgb) [package="5 mm [THT]"]
  R4 = Resistor [tolerance=±5% resistance=220 package=THT]
  R5 = Resistor [tolerance=±5% resistance=220 package=THT]
  L1 = Inductor [package="0603 [SMD]"]
  D1 = Rectifier Diode [package="Melf DO-213 AA [SMD]"]
  C1 = Capacitor [package=0805]
  C2 = Capacitor [package=0805]
  R6 = Resistor [tolerance=±5% resistance=220 package=THT]

nets:
  N1: Composant1.D5, R1.Pin_1
  N2: Composant1.D6, R3.Pin_1
  N3: Composant1.D7, R2.Pin_1
  N4: Composant1.D9, R4.Pin_1
  N5: Composant1.A0, D1.cathode, C1.1, R6.Pin_1
  N6: Composant1.5V, R5.Pin_0
  N7: R1.Pin_0, LED1.blue_anode
  N8: R2.Pin_0, LED1.red_anode
  N9: R3.Pin_0, LED1.green_anode
  N10: LED1.common_cathode, C1.2, R6.Pin_0
  N11: R4.Pin_0, R5.Pin_1, L1.pin_1
  N12: L1.pin_0, D1.anode, C2.2
